# Fritzing sketch Schema (saved by Fritzing 0.9.2b)
breadboards: 1

parts:
  Raspberry_Pi1 = Raspberry Pi B+
  LED1 = RGB LED (com. cathode, rbg) [package="5 mm [THT]"]
  R1 = Resistor [tolerance=±20% resistance=470 package="2512 [SMD]"]
  R2 = Resistor [tolerance=±20% resistance=470 package="2512 [SMD]"]
  R3 = Resistor [tolerance=±20% resistance=470 package="2512 [SMD]"]
  S1 = SWITCH-MOMENTARY-2 [package=tactile_switch_smd-2]

nets:
  N1: Raspberry_Pi1.GPIO22, R1.Pin_0
  N2: Raspberry_Pi1.GPIO18, S1.1
  N3: Raspberry_Pi1.GND, LED1.common_cathode
  N4: LED1.red_anode, R1.Pin_1
  N5: LED1.blue_anode, R2.Pin_1
  N6: LED1.green_anode, R3.Pin_1

notes:
  BUTTON
  PIN 12 (GPIO 18 in, #1)
  RGB LED
  R : PIN 15 (GPIO 22 out, #3)
  B : PIN 16 (GPIO 23 out, #4)
  G : PIN 18 (GPIO 24 out, #5)
